// Logisim project 1.circ as structural Verilog
module MyAND (
  input  in_1,
  input  in_2,
  output out_3
);

  wire nand_1_out;

  nand nand_1 (nand_1_out, in_1, in_2);
  not not_1 (out_3, nand_1_out);
endmodule

module myOR (
  input  in_1,
  input  in_2,
  output out_3
);

  wire and_1_out, not_1_out, not_2_out;

  not not_1 (not_1_out, in_1);
  not not_2 (not_2_out, in_2);
  not not_3 (out_3, and_1_out);
  and and_1 (and_1_out, not_1_out, not_2_out);
endmodule

module MyXOR (
  input  in_1,
  input  in_2,
  output out_3
);

  wire and_1_out, and_2_out, not_1_out, not_2_out;

  not not_1 (not_1_out, in_1);
  not not_2 (not_2_out, in_2);
  and and_1 (and_1_out, in_1, not_2_out);
  and and_2 (and_2_out, not_1_out, in_2);
  or or_1 (out_3, and_2_out, and_1_out);
endmodule

module MyNOT (
  input  in_1,
  output out_2
);

  not not_1 (out_2, in_1);
endmodule

module MyMultiplexor (
  input  in_1,
  input  in_2,
  output out_3,
  output out_4
);

  wire mynot_1_out_2;

  MyNOT mynot_1 (.in_1(in_1), .out_2(mynot_1_out_2));
  MyAND myand_1 (.in_1(mynot_1_out_2), .in_2(in_2), .out_3(out_3));
  MyAND myand_2 (.in_1(in_2), .in_2(in_1), .out_3(out_4));
endmodule

module myDemultiplexor (
  input  in_1,
  input  in_2,
  input  in_3,
  output out_4
);

  wire myand_1_out_3, myand_2_out_3, not_1_out;

  not not_1 (not_1_out, in_3);
  MyAND myand_1 (.in_1(in_1), .in_2(not_1_out), .out_3(myand_1_out_3));
  MyAND myand_2 (.in_1(in_2), .in_2(in_3), .out_3(myand_2_out_3));
  myOR myor_1 (.in_1(myand_1_out_3), .in_2(myand_2_out_3), .out_3(out_4));
endmodule

module myNOT4 (
  input  [3:0] in_1,
  output [3:0] out_2
);

  not not_1 (out_2[0], in_1[0]);
  not not_2 (out_2[1], in_1[1]);
  not not_3 (out_2[2], in_1[2]);
  not not_4 (out_2[3], in_1[3]);
endmodule

module myAND4 (
  input  [3:0] in_1,
  input  [3:0] in_2,
  output [3:0] out_3
);

  MyAND myand_1 (.in_1(in_1[0]), .in_2(in_2[0]), .out_3(out_3[0]));
  MyAND myand_2 (.in_1(in_2[1]), .in_2(in_1[1]), .out_3(out_3[1]));
  MyAND myand_3 (.in_1(in_2[2]), .in_2(in_1[2]), .out_3(out_3[2]));
  MyAND myand_4 (.in_1(in_1[3]), .in_2(in_2[3]), .out_3(out_3[3]));
endmodule

module myOR4 (
  input  [3:0] in_1,
  input  [3:0] in_2,
  output [3:0] out_3
);

  myOR myor_1 (.in_1(in_1[0]), .in_2(in_2[0]), .out_3(out_3[0]));
  myOR myor_2 (.in_1(in_1[1]), .in_2(in_2[1]), .out_3(out_3[1]));
  myOR myor_3 (.in_1(in_1[2]), .in_2(in_2[2]), .out_3(out_3[2]));
  myOR myor_4 (.in_1(in_1[3]), .in_2(in_2[3]), .out_3(out_3[3]));
endmodule

module myMUX4 (
  input  [3:0] in_1,
  input  [3:0] in_2,
  input  in_3,
  output [3:0] out_4
);

  myDemultiplexor mydemultiplexor_1 (.in_1(in_1[0]), .in_2(in_2[0]), .in_3(in_3), .out_4(out_4[0]));
  myDemultiplexor mydemultiplexor_2 (.in_1(in_1[1]), .in_2(in_2[1]), .in_3(in_3), .out_4(out_4[1]));
  myDemultiplexor mydemultiplexor_3 (.in_1(in_1[2]), .in_2(in_2[2]), .in_3(in_3), .out_4(out_4[2]));
  myDemultiplexor mydemultiplexor_4 (.in_1(in_1[3]), .in_2(in_2[3]), .in_3(in_3), .out_4(out_4[3]));
endmodule

module myDEMULT4 (
  input  [3:0] in_1,
  input  in_2,
  output [3:0] out_3,
  output [3:0] out_4
);

  MyMultiplexor mymultiplexor_1 (.in_1(in_2), .out_3(out_3[0]), .out_4(out_4[0]), .in_2(in_1[0]));
  MyMultiplexor mymultiplexor_2 (.in_1(in_2), .out_3(out_3[1]), .out_4(out_4[1]), .in_2(in_1[1]));
  MyMultiplexor mymultiplexor_3 (.in_1(in_2), .out_3(out_3[2]), .out_4(out_4[2]), .in_2(in_1[2]));
  MyMultiplexor mymultiplexor_4 (.in_1(in_2), .out_3(out_3[3]), .out_4(out_4[3]), .in_2(in_1[3]));
endmodule

module myOR8 (
  input  [3:0] in_1,
  output out_2
);

  wire myor_1_out_3, myor_2_out_3;

  myOR myor_1 (.in_1(in_1[0]), .in_2(in_1[1]), .out_3(myor_1_out_3));
  myOR myor_2 (.in_1(in_1[2]), .in_2(in_1[3]), .out_3(myor_2_out_3));
  myOR myor_3 (.in_1(myor_1_out_3), .in_2(myor_2_out_3), .out_3(out_2));
endmodule

module myMUX4WAY4 (
  input  [3:0] in_1,
  input  [3:0] in_2,
  input  [3:0] in_3,
  input  [3:0] in_4,
  input  [1:0] in_5,
  output [3:0] out_6
);

  wire [3:0] mymux4_1_out_4, mymux4_2_out_4;

  myMUX4 mymux4_1 (.in_1(in_1), .in_2(in_2), .out_4(mymux4_1_out_4), .in_3(in_5[0]));
  myMUX4 mymux4_2 (.in_1(in_3), .in_2(in_4), .out_4(mymux4_2_out_4), .in_3(in_5[0]));
  myMUX4 mymux4_3 (.in_1(mymux4_1_out_4), .in_2(mymux4_2_out_4), .out_4(out_6), .in_3(in_5[1]));
endmodule

module myMUX4WAY8 (
  input  [3:0] in_1,
  input  [3:0] in_2,
  input  [3:0] in_3,
  input  [3:0] in_4,
  input  [3:0] in_5,
  input  [3:0] in_6,
  input  [3:0] in_7,
  input  [3:0] in_8,
  input  [2:0] in_9,
  output [3:0] out_10
);

  wire [3:0] mymux4way4_1_out_6, mymux4way4_2_out_6;

  myMUX4WAY4 mymux4way4_1 (
    .in_1(in_1), .in_2(in_2), .in_3(in_3), .in_4(in_4), .out_6(mymux4way4_1_out_6), .in_5(in_9[1:0]));
  myMUX4WAY4 mymux4way4_2 (
    .in_1(in_5), .in_2(in_6), .in_3(in_7), .in_4(in_8), .out_6(mymux4way4_2_out_6), .in_5(in_9[1:0]));
  myMUX4 mymux4_1 (.in_1(mymux4way4_1_out_6), .in_2(mymux4way4_2_out_6), .out_4(out_10), .in_3(in_9[2]));
endmodule

module myDEMULT4WAY4 (
  input  [3:0] in_1,
  input  [1:0] in_2,
  output [3:0] out_3,
  output [3:0] out_4,
  output [3:0] out_5,
  output [3:0] out_6
);

  wire [3:0] mydemult4_1_out_3, mydemult4_1_out_4;

  myDEMULT4 mydemult4_1 (.in_1(in_1), .out_3(mydemult4_1_out_3), .out_4(mydemult4_1_out_4), .in_2(in_2[1]));
  myDEMULT4 mydemult4_2 (.in_1(mydemult4_1_out_3), .out_3(out_3), .out_4(out_4), .in_2(in_2[0]));
  myDEMULT4 mydemult4_3 (.in_1(mydemult4_1_out_4), .out_3(out_5), .out_4(out_6), .in_2(in_2[0]));
endmodule

module myDEMULT4WAY8 (
  input  [3:0] in_1,
  input  [2:0] in_2,
  output [3:0] out_3,
  output [3:0] out_4,
  output [3:0] out_5,
  output [3:0] out_6,
  output [3:0] out_7,
  output [3:0] out_8,
  output [3:0] out_9,
  output [3:0] out_10
);

  wire [3:0] mydemult4_1_out_3, mydemult4_1_out_4;

  myDEMULT4 mydemult4_1 (.in_1(in_1), .out_3(mydemult4_1_out_3), .out_4(mydemult4_1_out_4), .in_2(in_2[2]));
  myDEMULT4WAY4 mydemult4way4_1 (
    .in_1(mydemult4_1_out_3), .out_3(out_3), .out_4(out_4), .out_5(out_5), .out_6(out_6), .in_2(in_2[1:0]));
  myDEMULT4WAY4 mydemult4way4_2 (
    .in_1(mydemult4_1_out_4), .out_3(out_7), .out_4(out_8), .out_5(out_9), .out_6(out_10), .in_2(in_2[1:0]));
endmodule
