// Logisim project 2.circ as structural Verilog
module HalfAdder (
  input  in_1,
  input  in_2,
  output out_3,
  output out_4
);

  and and_1 (out_4, in_1, in_2);
  xor xor_1 (out_3, in_1, in_2);
endmodule

module FullAdder (
  input  in_1,
  input  in_2,
  input  in_3,
  output out_4,
  output out_5
);

  wire and_1_out, and_2_out, xor_1_out;

  and and_1 (and_1_out, in_2, in_3);
  or or_1 (out_5, and_1_out, and_2_out);
  xor xor_1 (xor_1_out, in_2, in_3);
  and and_2 (and_2_out, xor_1_out, in_1);
  xor xor_2 (out_4, in_1, xor_1_out);
endmodule

module N_Summarizer_4fee406a (
  input  [15:0] in_1,
  input  [15:0] in_2,
  input  in_3,
  output [15:0] out_4
);

  wire fulladder_1_out_5, fulladder_2_out_5, fulladder_3_out_5, fulladder_4_out_5, fulladder_5_out_5,
       fulladder_6_out_5, fulladder_7_out_5, fulladder_8_out_5, fulladder_9_out_5, fulladder_10_out_5,
       fulladder_11_out_5, fulladder_12_out_5, fulladder_13_out_5, fulladder_14_out_5, fulladder_15_out_5;

  FullAdder fulladder_1 (.in_2(in_1[0]), .in_3(in_3), .out_4(out_4[0]), .in_1(in_2[0]), .out_5(fulladder_1_out_5));
  FullAdder fulladder_2 (
    .in_2(in_2[1]), .in_3(in_1[1]), .out_4(out_4[1]), .in_1(fulladder_1_out_5), .out_5(fulladder_2_out_5));
  FullAdder fulladder_3 (
    .in_2(in_2[2]), .in_3(in_1[2]), .out_4(out_4[2]), .in_1(fulladder_2_out_5), .out_5(fulladder_3_out_5));
  FullAdder fulladder_4 (
    .in_2(in_2[3]), .in_3(in_1[3]), .out_4(out_4[3]), .in_1(fulladder_3_out_5), .out_5(fulladder_4_out_5));
  FullAdder fulladder_5 (
    .in_2(in_2[4]), .in_3(in_1[4]), .out_4(out_4[4]), .in_1(fulladder_4_out_5), .out_5(fulladder_5_out_5));
  FullAdder fulladder_6 (
    .in_2(in_2[5]), .in_3(in_1[5]), .out_4(out_4[5]), .in_1(fulladder_5_out_5), .out_5(fulladder_6_out_5));
  FullAdder fulladder_7 (
    .in_2(in_2[6]), .in_3(in_1[6]), .out_4(out_4[6]), .in_1(fulladder_6_out_5), .out_5(fulladder_7_out_5));
  FullAdder fulladder_8 (
    .in_2(in_2[7]), .in_3(in_1[7]), .out_4(out_4[7]), .in_1(fulladder_7_out_5), .out_5(fulladder_8_out_5));
  FullAdder fulladder_9 (
    .in_2(in_2[8]), .in_3(in_1[8]), .out_4(out_4[8]), .in_1(fulladder_8_out_5), .out_5(fulladder_9_out_5));
  FullAdder fulladder_10 (
    .in_2(in_2[9]), .in_3(in_1[9]), .out_4(out_4[9]), .in_1(fulladder_9_out_5), .out_5(fulladder_10_out_5));
  FullAdder fulladder_11 (
    .in_2(in_2[10]), .in_3(in_1[10]), .out_4(out_4[10]), .in_1(fulladder_10_out_5), .out_5(fulladder_11_out_5));
  FullAdder fulladder_12 (
    .in_2(in_2[11]), .in_3(in_1[11]), .out_4(out_4[11]), .in_1(fulladder_11_out_5), .out_5(fulladder_12_out_5));
  FullAdder fulladder_13 (
    .in_2(in_2[12]), .in_3(in_1[12]), .out_4(out_4[12]), .in_1(fulladder_12_out_5), .out_5(fulladder_13_out_5));
  FullAdder fulladder_14 (
    .in_2(in_2[13]), .in_3(in_1[13]), .out_4(out_4[13]), .in_1(fulladder_13_out_5), .out_5(fulladder_14_out_5));
  FullAdder fulladder_15 (
    .in_2(in_2[14]), .in_3(in_1[14]), .out_4(out_4[14]), .in_1(fulladder_14_out_5), .out_5(fulladder_15_out_5));
  FullAdder fulladder_16 (
    .in_2(in_2[15]), .in_3(in_1[15]), .out_4(out_4[15]), .in_1(fulladder_15_out_5));  // open: out_5
endmodule

module Incrementer (
  input  [3:0] in_1,
  output [3:0] out_2
);

  Adder #(.width(4)) adder_1 (.a(in_1), .b(4'b0001), .out(out_2));  // open: cin, cout
endmodule

module Subtraction (
  input  [15:0] in_1,
  input  [15:0] in_2,
  input  in_3,
  output [15:0] out_4
);

  wire [15:0] not_1_out;

  assign not_1_out = ~in_1;  // NOT_Gate not_1, 16 bits wide
  N_Summarizer_4fee406a n_summarizer_4fee406a_1 (.in_1(in_2), .in_2(not_1_out), .in_3(in_3), .out_4(out_4));
endmodule

module InDeCrementor (
  input  in_1,
  input  [3:0] in_2,
  input  [3:0] in_3,
  output [3:0] out_4
);

  wire fulladder_1_out_5, fulladder_2_out_5, fulladder_3_out_5;
  wire [3:0] multiplexer_1_out, not_1_out;

  assign not_1_out = ~in_2;  // NOT_Gate not_1, 4 bits wide
  Multiplexer #(.width(4), .enable("false")) multiplexer_1 (
    .in0(in_2), .in1(not_1_out), .out(multiplexer_1_out), .sel(in_1));
  FullAdder fulladder_1 (
    .in_2(in_3[0]), .in_3(in_1), .out_4(out_4[0]), .in_1(multiplexer_1_out[0]), .out_5(fulladder_1_out_5));
  FullAdder fulladder_2 (
    .in_2(multiplexer_1_out[1]), .in_3(in_3[1]), .out_4(out_4[1]), .in_1(fulladder_1_out_5),
    .out_5(fulladder_2_out_5));
  FullAdder fulladder_3 (
    .in_2(multiplexer_1_out[2]), .in_3(in_3[2]), .out_4(out_4[2]), .in_1(fulladder_2_out_5),
    .out_5(fulladder_3_out_5));
  FullAdder fulladder_4 (
    .in_2(multiplexer_1_out[3]), .in_3(in_3[3]), .out_4(out_4[3]), .in_1(fulladder_3_out_5));  // open: out_5
endmodule

module EqualityComparator (
  input  [3:0] in_1,
  input  [3:0] in_2,
  output out_3
);

  wire xnor_1_out, xnor_2_out, xnor_3_out, xnor_4_out;

  xnor xnor_1 (xnor_1_out, in_1[0], in_2[0]);
  xnor xnor_2 (xnor_2_out, in_1[1], in_2[1]);
  xnor xnor_3 (xnor_3_out, in_1[2], in_2[2]);
  xnor xnor_4 (xnor_4_out, in_1[3], in_2[3]);
  and and_1 (out_3, xnor_1_out, xnor_2_out, xnor_3_out, xnor_4_out);
endmodule

module MagnitudeComparator (
  input  [15:0] in_1,
  input  [15:0] in_2,
  input  in_3,
  output out_4
);

  wire [15:0] subtraction_1_out_4;

  Subtraction subtraction_1 (.in_1(in_1), .in_2(in_2), .in_3(in_3), .out_4(subtraction_1_out_4));
  xor xor_1 (out_4, subtraction_1_out_4[15], in_3);
endmodule

module SHIFT_2_LEFT (
  input  [1:0] in_1,
  input  in_2,
  input  [3:0] in_3,
  output [3:0] out_4
);

  Multiplexer #(.select(2), .enable("false")) multiplexer_1 (
    .in0(in_3[3]), .in1(in_3[2]), .in2(in_3[1]), .in3(in_3[0]), .out(out_4[0]), .sel(in_1));
  Multiplexer #(.select(2), .enable("false")) multiplexer_2 (
    .in0(in_3[2]), .in1(in_3[1]), .in2(in_3[0]), .in3(in_2), .out(out_4[1]), .sel(in_1));
  Multiplexer #(.select(2), .enable("false")) multiplexer_3 (
    .in0(in_3[1]), .in1(in_3[0]), .in2(in_2), .in3(in_2), .out(out_4[2]), .sel(in_1));
  Multiplexer #(.select(2), .enable("false")) multiplexer_4 (
    .in0(in_3[0]), .in1(in_2), .in2(in_2), .in3(in_2), .out(out_4[3]), .sel(in_1));
endmodule

module SHIFT_2_RIGHT (
  input  in_1,
  input  [1:0] in_2,
  input  [3:0] in_3,
  output [3:0] out_4
);

  Multiplexer #(.select(2), .enable("false")) multiplexer_1 (
    .in0(in_3[3]), .in1(in_1), .in2(in_1), .in3(in_1), .out(out_4[3]), .sel(in_2));
  Multiplexer #(.select(2), .enable("false")) multiplexer_2 (
    .in0(in_3[2]), .in1(in_3[3]), .in2(in_1), .in3(in_1), .out(out_4[2]), .sel(in_2));
  Multiplexer #(.select(2), .enable("false")) multiplexer_3 (
    .in0(in_3[1]), .in1(in_3[2]), .in2(in_3[3]), .in3(in_1), .out(out_4[1]), .sel(in_2));
  Multiplexer #(.select(2), .enable("false")) multiplexer_4 (
    .in0(in_3[0]), .in1(in_3[1]), .in2(in_3[2]), .in3(in_3[3]), .out(out_4[0]), .sel(in_2));
endmodule

module ROTATOR (
  input  [1:0] in_1,
  input  [3:0] in_2,
  output [3:0] out_3
);

  Multiplexer #(.select(2), .enable("false")) multiplexer_1 (
    .in0(in_2[0]), .in1(in_2[0]), .in2(in_2[0]), .in3(in_2[0]), .out(out_3[3]), .sel(in_1));
  Multiplexer #(.select(2), .enable("false")) multiplexer_2 (
    .in0(in_2[1]), .in1(in_2[0]), .in2(in_2[0]), .in3(in_2[0]), .out(out_3[2]), .sel(in_1));
  Multiplexer #(.select(2), .enable("false")) multiplexer_3 (
    .in0(in_2[2]), .in1(in_2[1]), .in2(in_2[0]), .in3(in_2[0]), .out(out_3[1]), .sel(in_1));
  Multiplexer #(.select(2), .enable("false")) multiplexer_4 (
    .in0(in_2[3]), .in1(in_2[2]), .in2(in_2[1]), .in3(in_2[0]), .out(out_3[0]), .sel(in_1));
endmodule

module ALU (
  input  [2:0] in_1,
  input  [3:0] in_2,
  input  [3:0] in_3,
  input  [1:0] in_4,
  output out_5,
  output [3:0] out_6
);

  wire bitselector_1_out;
  wire [3:0] and_1_out, bit_extender_1_out, multiplexer_1_out, not_1_out, or_1_out, summ4_1_out_4;

  assign not_1_out = ~in_2;  // NOT_Gate not_1, 4 bits wide
  Multiplexer #(.width(4), .enable("false")) multiplexer_1 (
    .in0(in_2), .in1(not_1_out), .out(multiplexer_1_out), .sel(in_1[2]));
  SUMM4 summ4_1 (.in_2(in_3), .in_3(multiplexer_1_out), .out_4(summ4_1_out_4), .in_1(in_1[2]));
  assign and_1_out = multiplexer_1_out & in_3;  // AND_Gate and_1, 4 bits wide
  assign or_1_out = multiplexer_1_out | in_3;  // OR_Gate or_1, 4 bits wide
  BitSelector #(.width(4)) bitselector_1 (.in(summ4_1_out_4), .out(bitselector_1_out), .sel(in_4));
  assign bit_extender_1_out = {{3{bitselector_1_out}}, bitselector_1_out};  // Bit_Extender bit_extender_1
  Multiplexer #(.select(2), .width(4), .enable("false")) multiplexer_2 (
    .in0(and_1_out), .in1(or_1_out), .in2(summ4_1_out_4), .in3(bit_extender_1_out), .out(out_6),
    .sel(in_1[1:0]));
  nor nor_1 (out_5, out_6[0], out_6[1], out_6[2], out_6[3]);
endmodule

module SUMM4 (
  input  in_1,
  input  [3:0] in_2,
  input  [3:0] in_3,
  output [3:0] out_4
);

  wire fulladder_1_out_5, fulladder_2_out_5, fulladder_3_out_5;

  FullAdder fulladder_1 (.in_2(in_3[0]), .in_3(in_1), .out_4(out_4[0]), .in_1(in_2[0]), .out_5(fulladder_1_out_5));
  FullAdder fulladder_2 (
    .in_2(in_2[1]), .in_3(in_3[1]), .out_4(out_4[1]), .in_1(fulladder_1_out_5), .out_5(fulladder_2_out_5));
  FullAdder fulladder_3 (
    .in_2(in_2[2]), .in_3(in_3[2]), .out_4(out_4[2]), .in_1(fulladder_2_out_5), .out_5(fulladder_3_out_5));
  FullAdder fulladder_4 (.in_2(in_2[3]), .in_3(in_3[3]), .out_4(out_4[3]), .in_1(fulladder_3_out_5));  // open: out_5
endmodule

module ALU_Extended (
  input  [5:0] in_1,
  input  [15:0] x,
  input  [15:0] y,
  output [15:0] out_4,
  output ng,
  output zr
);

  wire or_1_out;
  wire [15:0] adder_1_out, and_1_out, multiplexer_1_out, multiplexer_2_out, multiplexer_3_out,
       multiplexer_4_out, multiplexer_5_out, not_1_out, not_2_out, not_3_out;

  Multiplexer #(.width(16), .enable("false")) multiplexer_1 (
    .in0(x), .in1({16{1'b0}}), .out(multiplexer_1_out), .sel(in_1[5]));
  Multiplexer #(.width(16), .enable("false")) multiplexer_2 (
    .in0(y), .in1({16{1'b0}}), .out(multiplexer_2_out), .sel(in_1[3]));
  assign not_1_out = ~multiplexer_1_out;  // NOT_Gate not_1, 16 bits wide
  assign not_2_out = ~multiplexer_2_out;  // NOT_Gate not_2, 16 bits wide
  Multiplexer #(.width(16), .enable("false")) multiplexer_3 (
    .in0(multiplexer_1_out), .in1(not_1_out), .out(multiplexer_3_out), .sel(in_1[4]));
  Multiplexer #(.width(16), .enable("false")) multiplexer_4 (
    .in0(multiplexer_2_out), .in1(not_2_out), .out(multiplexer_4_out), .sel(in_1[2]));
  assign and_1_out = multiplexer_3_out & multiplexer_4_out;  // AND_Gate and_1, 16 bits wide
  Adder #(.width(16)) adder_1 (
    .a(multiplexer_3_out), .b(multiplexer_4_out), .out(adder_1_out), .cout(ng));  // open: cin
  Multiplexer #(.width(16), .enable("false")) multiplexer_5 (
    .in0(and_1_out), .in1(adder_1_out), .out(multiplexer_5_out), .sel(in_1[1]));
  Multiplexer #(.width(16), .enable("false")) multiplexer_6 (
    .in0(multiplexer_5_out), .in1(not_3_out), .out(out_4), .sel(in_1[0]));
  assign not_3_out = ~multiplexer_5_out;  // NOT_Gate not_3, 16 bits wide
  or or_1 (or_1_out, out_4[15], out_4[14], out_4[13], out_4[12], out_4[11], out_4[10], out_4[9], out_4[8], out_4[7], out_4[6], out_4[5], out_4[4], out_4[3], out_4[2], out_4[1], out_4[0]);
  not not_4 (zr, or_1_out);
endmodule
