// Logisim project 3.circ as structural Verilog: 20 circuits, main circuit main
module main (
  input  in_1,
  input  in_2,
  input  in_3,
  input  in_4,
  output out_5,
  output out_6
);

  D_Flip_Flop d_ff_1 (.D(in_2), .clk(in_3), .Q(out_5), .Qn(out_6), .preset(in_1), .reset(in_4));
endmodule

module srlatch (
  input  R,
  input  S,
  output Q,
  output Qp
);

  nor nor_1 (Q, R, Qp);
  nor nor_2 (Qp, Q, S);
endmodule

module dlatch (
  input  CLK,
  input  D,
  output Q,
  output Qp
);

  wire and_1_out, and_2_out, not_1_out;

  not not_1 (not_1_out, D);
  and and_1 (and_1_out, CLK, not_1_out);
  and and_2 (and_2_out, CLK, D);
  srlatch srlatch_1 (.Qp(Qp), .Q(Q), .S(and_2_out), .R(and_1_out));
endmodule

module dfilpflop (
  input  CLK,
  input  D,
  output Q
);

  wire dlatch_1_q, not_1_out;

  not not_1 (not_1_out, CLK);
  dlatch dlatch_1 (.Q(dlatch_1_q), .D(D), .CLK(not_1_out));  // open: Qp
  dlatch dlatch_2 (.Q(Q), .D(dlatch_1_q), .CLK(CLK));  // open: Qp
endmodule

module enabled (
  input  CLK,
  input  EN,
  input  D,
  output Q
);

  wire and_1_out;

  and and_1 (and_1_out, CLK, EN);
  dfilpflop dfilpflop_1 (.Q(Q), .D(D), .CLK(and_1_out));
endmodule

module resetable (
  input  CLK,
  input  D,
  input  RESET,
  output Q
);

  wire and_1_out, not_1_out;

  and and_1 (and_1_out, D, not_1_out);
  not not_1 (not_1_out, RESET);
  dfilpflop dfilpflop_1 (.Q(Q), .D(and_1_out), .CLK(CLK));
endmodule

module async_reset_dlatch (
  input  CLK,
  input  D,
  input  RESET,
  output Q,
  output Qp
);

  wire and_1_out, and_2_out, and_3_out, not_1_out, not_2_out, or_1_out;

  not not_1 (not_1_out, RESET);
  or or_1 (or_1_out, CLK, RESET);
  and and_1 (and_1_out, D, not_1_out);
  not not_2 (not_2_out, and_1_out);
  and and_2 (and_2_out, or_1_out, not_2_out);
  and and_3 (and_3_out, or_1_out, and_1_out);
  srlatch srlatch_1 (.Qp(Qp), .Q(Q), .S(and_3_out), .R(and_2_out));
endmodule

module async_reset_dflipflop (
  input  CLK,
  input  D,
  input  RESET,
  output Q
);

  wire async_reset_dlatch_1_q, not_1_out, or_1_out;

  not not_1 (not_1_out, or_1_out);
  async_reset_dlatch async_reset_dlatch_1 (
    .RESET(RESET), .Q(async_reset_dlatch_1_q), .D(D), .CLK(not_1_out));  // open: Qp
  or or_1 (or_1_out, RESET, CLK);
  dlatch dlatch_1 (.Q(Q), .D(async_reset_dlatch_1_q), .CLK(or_1_out));  // open: Qp
endmodule

module setable (
  input  CLK,
  input  D,
  input  SET,
  output out_4
);

  wire or_1_out;

  or or_1 (or_1_out, D, SET);
  dfilpflop dfilpflop_1 (.Q(out_4), .D(or_1_out), .CLK(CLK));
endmodule

module async_set_dlatch (
  input  CLK,
  input  D,
  input  SET,
  output Q,
  output Qp
);

  wire and_1_out, and_2_out, not_1_out, or_1_out, or_2_out;

  or or_1 (or_1_out, CLK, SET);
  or or_2 (or_2_out, D, SET);
  not not_1 (not_1_out, or_2_out);
  and and_1 (and_1_out, or_1_out, not_1_out);
  and and_2 (and_2_out, or_1_out, or_2_out);
  srlatch srlatch_1 (.Qp(Qp), .Q(Q), .S(and_2_out), .R(and_1_out));
endmodule

module async_set_dflipflop (
  input  CLK,
  input  D,
  input  SET,
  output out_4
);

  wire async_set_dlatch_1_q, not_1_out, or_1_out;

  not not_1 (not_1_out, or_1_out);
  async_set_dlatch async_set_dlatch_1 (.Q(async_set_dlatch_1_q), .SET(SET), .D(D), .CLK(not_1_out));  // open: Qp
  or or_1 (or_1_out, SET, CLK);
  dlatch dlatch_1 (.Q(out_4), .D(async_set_dlatch_1_q), .CLK(or_1_out));  // open: Qp
endmodule

module toWrite (
  input  d,
  input  s,
  input  r,
  output x
);

  wire and_1_out, and_2_out, and_3_out, not_1_out, not_2_out;

  not not_1 (not_1_out, r);
  not not_2 (not_2_out, r);
  and and_1 (and_1_out, s, not_1_out);
  and and_2 (and_2_out, d, not_2_out);
  and and_3 (and_3_out, d, s);
  or or_1 (x, and_1_out, and_2_out, and_3_out);
endmodule

module async_rs_dlatch (
  input  CLK,
  input  D,
  input  SET,
  input  RESET,
  output Q,
  output Qp
);

  wire and_1_out, and_2_out, not_1_out, or_1_out, towrite_1_x;

  or or_1 (or_1_out, CLK, SET, RESET);
  not not_1 (not_1_out, towrite_1_x);
  toWrite towrite_1 (.d(D), .s(SET), .r(RESET), .x(towrite_1_x));
  and and_1 (and_1_out, or_1_out, not_1_out);
  and and_2 (and_2_out, or_1_out, towrite_1_x);
  srlatch srlatch_1 (.Qp(Qp), .Q(Q), .S(and_2_out), .R(and_1_out));
endmodule

module DFLIPFLOP (
  input  CLK,
  input  EN,
  input  D,
  input  SET,
  input  RESET,
  output Q
);

  wire and_1_out, async_rs_dlatch_1_q, not_1_out, or_1_out;

  not not_1 (not_1_out, and_1_out);
  or or_1 (or_1_out, RESET, SET, CLK);
  and and_1 (and_1_out, or_1_out, EN);
  async_rs_dlatch async_rs_dlatch_1 (
    .Q(async_rs_dlatch_1_q), .RESET(RESET), .SET(SET), .D(D), .CLK(not_1_out));  // open: Qp
  dlatch dlatch_1 (.Q(Q), .D(async_rs_dlatch_1_q), .CLK(and_1_out));  // open: Qp
endmodule

module Register4 (
  input  CLK,
  input  [3:0] X,
  output [3:0] Y
);

  dfilpflop dfilpflop_1 (.Q(Y[0]), .D(X[0]), .CLK(CLK));
  dfilpflop dfilpflop_2 (.Q(Y[1]), .D(X[1]), .CLK(CLK));
  dfilpflop dfilpflop_3 (.Q(Y[2]), .D(X[2]), .CLK(CLK));
  dfilpflop dfilpflop_4 (.Q(Y[3]), .D(X[3]), .CLK(CLK));
endmodule

module scheme1 (
  input  [7:0] A,
  input  [7:0] B,
  input  C,
  input  CLK
);

  wire [7:0] adder_1_out, register_1_q, register_2_q, xor_1_out;

  assign xor_1_out = A ^ B;  // XOR_Gate xor_1, 8 bits wide
  Adder adder_1 (.a(register_2_q), .b(xor_1_out), .out(adder_1_out), .cin(C));  // open: cout
  Register register_1 (.D(adder_1_out), .en(CLK), .clk(CLK), .Q(register_1_q));  // open: clr
  Register register_2 (.D(register_1_q), .en(CLK), .clk(CLK), .Q(register_2_q));  // open: clr

  // Notes on the sheet:
  //   0x3 0x5
  //   0x8 0x3
  //   0x6 0x8
  //   0xb 0x6
  //   0x9 0xb
endmodule

module scheme2 (
  input  [7:0] I,
  input  in_2,
  output [7:0] O
);

  wire button_1_out, clock_1_out;
  wire [7:0] adder_1_out, multiplexer_1_out, not_1_out;

  assign not_1_out = ~I;  // NOT_Gate not_1, 8 bits wide
  Button button_1 (.out(button_1_out));
  Multiplexer #(.width(8), .enable("false")) multiplexer_1 (
    .in0(I), .in1(not_1_out), .out(multiplexer_1_out), .sel(button_1_out));
  Adder adder_1 (.a(multiplexer_1_out), .b(O), .out(adder_1_out));  // open: cin, cout
  Clock clock_1 (.out(clock_1_out));
  Register register_1 (.D(adder_1_out), .en(clock_1_out), .clk(clock_1_out), .Q(O), .clr(in_2));
endmodule

module RAM8 (
  input  CLK,
  input  [31:0] i,
  input  load,
  input  [2:0] address,
  output [31:0] o
);

  wire demultiplexer_1_out0, demultiplexer_1_out1, demultiplexer_1_out2, demultiplexer_1_out3,
       demultiplexer_1_out4, demultiplexer_1_out5, demultiplexer_1_out6, demultiplexer_1_out7;
  wire [31:0] register_1_q, register_2_q, register_3_q, register_4_q, register_5_q, register_6_q,
       register_7_q, register_8_q;

  Demultiplexer #(.select(3), .enable("false")) demultiplexer_1 (
    .out0(demultiplexer_1_out0), .out1(demultiplexer_1_out1), .out2(demultiplexer_1_out2),
    .out3(demultiplexer_1_out3), .out4(demultiplexer_1_out4), .out5(demultiplexer_1_out5),
    .out6(demultiplexer_1_out6), .out7(demultiplexer_1_out7), .in(load), .sel(address));
  Register #(.width(32)) register_1 (.D(i), .en(demultiplexer_1_out0), .clk(CLK), .Q(register_1_q));  // open: clr
  Register #(.width(32)) register_2 (.D(i), .en(demultiplexer_1_out1), .clk(CLK), .Q(register_2_q));  // open: clr
  Register #(.width(32)) register_3 (.D(i), .en(demultiplexer_1_out2), .clk(CLK), .Q(register_3_q));  // open: clr
  Register #(.width(32)) register_4 (.D(i), .en(demultiplexer_1_out3), .clk(CLK), .Q(register_4_q));  // open: clr
  Register #(.width(32)) register_5 (.D(i), .en(demultiplexer_1_out4), .clk(CLK), .Q(register_5_q));  // open: clr
  Register #(.width(32)) register_6 (.D(i), .en(demultiplexer_1_out5), .clk(CLK), .Q(register_6_q));  // open: clr
  Register #(.width(32)) register_7 (.D(i), .en(demultiplexer_1_out6), .clk(CLK), .Q(register_7_q));  // open: clr
  Register #(.width(32)) register_8 (.D(i), .en(demultiplexer_1_out7), .clk(CLK), .Q(register_8_q));  // open: clr
  Multiplexer #(.select(3), .width(32), .enable("false")) multiplexer_1 (
    .in0(register_1_q), .in1(register_2_q), .in2(register_3_q), .in3(register_4_q), .in4(register_5_q),
    .in5(register_6_q), .in6(register_7_q), .in7(register_8_q), .out(o), .sel(address));
endmodule

module RAM64 (
  input  [31:0] i,
  input  load,
  input  [5:0] address,
  output [31:0] out_4
);

  wire clock_1_out, demultiplexer_1_out0, demultiplexer_1_out1, demultiplexer_1_out2, demultiplexer_1_out3,
       demultiplexer_1_out4, demultiplexer_1_out5, demultiplexer_1_out6, demultiplexer_1_out7;
  wire [31:0] ram8_1_o, ram8_2_o, ram8_3_o, ram8_4_o, ram8_5_o, ram8_6_o, ram8_7_o, ram8_8_o;

  Demultiplexer #(.select(3), .enable("false")) demultiplexer_1 (
    .out0(demultiplexer_1_out0), .out1(demultiplexer_1_out1), .out2(demultiplexer_1_out2),
    .out3(demultiplexer_1_out3), .out4(demultiplexer_1_out4), .out5(demultiplexer_1_out5),
    .out6(demultiplexer_1_out6), .out7(demultiplexer_1_out7), .in(load), .sel(address[2:0]));
  Clock clock_1 (.out(clock_1_out));
  RAM8 ram8_1 (.CLK(clock_1_out), .i(i), .load(demultiplexer_1_out0), .address(address[5:3]), .o(ram8_1_o));
  RAM8 ram8_2 (.CLK(clock_1_out), .i(i), .load(demultiplexer_1_out1), .address(address[5:3]), .o(ram8_2_o));
  RAM8 ram8_3 (.CLK(clock_1_out), .i(i), .load(demultiplexer_1_out2), .address(address[5:3]), .o(ram8_3_o));
  RAM8 ram8_4 (.CLK(clock_1_out), .i(i), .load(demultiplexer_1_out3), .address(address[5:3]), .o(ram8_4_o));
  RAM8 ram8_5 (.CLK(clock_1_out), .i(i), .load(demultiplexer_1_out4), .address(address[5:3]), .o(ram8_5_o));
  RAM8 ram8_6 (.CLK(clock_1_out), .i(i), .load(demultiplexer_1_out5), .address(address[5:3]), .o(ram8_6_o));
  RAM8 ram8_7 (.CLK(clock_1_out), .i(i), .load(demultiplexer_1_out6), .address(address[5:3]), .o(ram8_7_o));
  RAM8 ram8_8 (.CLK(clock_1_out), .i(i), .load(demultiplexer_1_out7), .address(address[5:3]), .o(ram8_8_o));
  Multiplexer #(.select(3), .width(32), .enable("false")) multiplexer_1 (
    .in0(ram8_1_o), .in1(ram8_2_o), .in2(ram8_3_o), .in3(ram8_4_o), .in4(ram8_5_o), .in5(ram8_6_o),
    .in6(ram8_7_o), .in7(ram8_8_o), .out(out_4), .sel(address[2:0]));
endmodule

module PC (
  input  load,
  input  inc,
  input  reset,
  input  [15:0] i,
  output [15:0] o
);

  wire clock_1_out, not_1_out, or_1_out;
  wire [15:0] adder_1_out, multiplexer_1_out;

  not not_1 (not_1_out, load);
  Multiplexer #(.width(16), .enable("false")) multiplexer_1 (
    .in0(i), .in1(adder_1_out), .out(multiplexer_1_out), .sel(not_1_out));
  or or_1 (or_1_out, inc, load);
  Clock clock_1 (.out(clock_1_out));
  Register #(.width(16)) register_1 (.D(multiplexer_1_out), .en(or_1_out), .clk(clock_1_out), .Q(o), .clr(reset));
  Adder #(.width(16)) adder_1 (.a(o), .b(16'h1), .out(adder_1_out));  // open: cin, cout
endmodule
