// Logisim project 5.circ as structural Verilog
module main (
  input  in_1,
  output [31:0] out_2
);

  wire clock_1_out;
  wire [31:0] pc_1_addr;

  Clock clock_1 (.out(clock_1_out));
  PC pc_1 (.CLK(clock_1_out), .Reset(in_1), .addr(pc_1_addr));
  // MIPSProgramROM mipsprogramrom_1: pin names not known; wires that end beside it: pc_1_addr, out_2

  // Notes on the sheet:
  //   contents of mipsprogramrom_1 (hex, n*v repeats v):
  //   ADDIU $2, $0, 0x38 ADDIU $3, $0, 0x8 ADDIU $4, $0, 0x2 ADDIU $5, $0, 0x1  SLTI $6, $2, 0xf SLTI $7,
  //   $3, 0x8 SLTI $8, $1, 0x80 SLTI $9, $2, 0x800
endmodule

module PC (
  input  CLK,
  input  Reset,
  output [31:0] addr
);

  wire [31:0] adder_1_out;

  Register #(.width(32)) register_1 (.D(adder_1_out), .clk(CLK), .Q(addr), .clr(Reset));  // open: en
  Adder #(.width(32)) adder_1 (.a(addr), .b(32'h4), .out(adder_1_out));  // open: cin, cout
endmodule

module Decode (
  input  [31:0] instruction,
  output [5:0] funct,
  output [4:0] shamt,
  output [4:0] rd,
  output [4:0] rt,
  output [4:0] rs,
  output [5:0] opcode,
  output [15:0] imm,
  output [25:0] addr
);


  assign addr = instruction[25:0];
  assign funct = instruction[5:0];
  assign imm = instruction[15:0];
  assign opcode = instruction[31:26];
  assign rd = instruction[15:11];
  assign rs = instruction[25:21];
  assign rt = instruction[20:16];
  assign shamt = instruction[10:6];
endmodule

module Control (
  input  [5:0] opcode,
  output [3:0] ALUOp,
  output RegWrite,
  output ExOp,
  output SLTOp
);

  o_alu o_alu_1 (
    .x5(opcode[5]), .x4(opcode[4]), .x3(opcode[3]), .x2(opcode[2]), .x1(opcode[1]), .x0(opcode[0]),
    .a3(ALUOp[3]), .a2(ALUOp[2]), .a1(ALUOp[1]), .a0(ALUOp[0]));
  o_oth o_oth_1 (
    .x5(opcode[5]), .x4(opcode[4]), .x3(opcode[3]), .x2(opcode[2]), .x1(opcode[1]), .x0(opcode[0]),
    .RegWrite(RegWrite), .ExOp(ExOp), .SLTOp(SLTOp));
endmodule

module o_alu (
  input  x5,
  input  x4,
  input  x3,
  input  x2,
  input  x1,
  input  x0,
  output a3,
  output a2,
  output a1,
  output a0
);


  assign a0 = 1'b0;
  assign a1 = x0;
  assign a2 = x1;
  assign a3 = x2;
endmodule

module o_oth (
  input  x5,
  input  x4,
  input  x3,
  input  x2,
  input  x1,
  input  x0,
  output RegWrite,
  output ExOp,
  output SLTOp
);

  wire and_1_out, and_2_out, not_1_out, not_2_out, not_3_out, not_4_out, not_5_out;

  not not_1 (not_1_out, x2);
  not not_2 (not_2_out, x1);
  not not_3 (not_3_out, x2);
  not not_4 (not_4_out, x0);
  not not_5 (not_5_out, x2);
  and and_1 (and_1_out, not_1_out, not_2_out);
  and and_2 (and_2_out, not_3_out, not_4_out);
  and and_3 (SLTOp, not_5_out, x1);
  or or_1 (ExOp, and_1_out, and_2_out);

  assign RegWrite = 1'b1;
endmodule

module ADDIU (
  input  CLK,
  input  in_2
);

  wire registerfile_1_p1, registerfile_1_p3, registerfile_1_p6;
  wire [3:0] control_1_aluop;
  wire [4:0] decode_1_rs, decode_1_rt;
  wire [5:0] decode_1_opcode;
  wire [15:0] decode_1_imm;
  wire [31:0] bit_extender_1_out, mipsprogramrom_1_p2, pc_1_addr;

  PC pc_1 (.CLK(CLK), .Reset(in_2), .addr(pc_1_addr));
  Decode decode_1 (
    .instruction(mipsprogramrom_1_p2), .rt(decode_1_rt), .rs(decode_1_rs), .opcode(decode_1_opcode),
    .imm(decode_1_imm));  // open: funct, shamt, rd, addr
  // MIPSProgramROM mipsprogramrom_1: pin names not known; wires that end beside it: pc_1_addr, mipsprogramrom_1_p2
  assign bit_extender_1_out = {{16{decode_1_imm[15]}}, decode_1_imm};  // Bit_Extender bit_extender_1
  // RegisterFile registerfile_1: pin names not known; wires that end beside it: registerfile_1_p1, CLK, registerfile_1_p3, decode_1_rt, decode_1_rs, registerfile_1_p6
  Control control_1 (
    .opcode(decode_1_opcode), .ALUOp(control_1_aluop), .RegWrite(registerfile_1_p3));  // open: ExOp, SLTOp
  // Mips_ALU mips_alu_1: pin names not known; wires that end beside it: registerfile_1_p6, bit_extender_1_out, control_1_aluop, registerfile_1_p1

  // Notes on the sheet:
  //   contents of mipsprogramrom_1 (hex, n*v repeats v):
  //   ADDIU $2, $0, 0x38 ADDIU $3, $0, 0x8 ADDIU $4, $0, 0x2 ADDIU $5, $0, 0x1
endmodule

module bit_extend (
  input  [15:0] imm,
  input  ExOp,
  output [31:0] y
);

  wire [31:0] bit_extender_1_out, bit_extender_2_out;

  assign bit_extender_1_out = {{16{1'b0}}, imm};  // Bit_Extender bit_extender_1
  assign bit_extender_2_out = {{16{imm[15]}}, imm};  // Bit_Extender bit_extender_2
  Multiplexer #(.width(32), .enable("false")) multiplexer_1 (
    .in0(bit_extender_1_out), .in1(bit_extender_2_out), .out(y), .sel(ExOp));
endmodule

module number_7 (
  input  Reset
);

  wire CLK_out, control_1_exop, control_1_sltop, registerfile_1_p3, slt_1_y;
  wire [3:0] control_1_aluop;
  wire [4:0] decode_1_rs, decode_1_rt;
  wire [5:0] decode_1_opcode;
  wire [15:0] decode_1_imm;
  wire [31:0] bit_extend_1_y, bit_extender_1_out, mips_alu_1_p4, mipsprogramrom_1_p2, pc_1_addr,
       registerfile_1_p1, registerfile_1_p6;

  Clock CLK (.out(CLK_out));
  PC pc_1 (.CLK(CLK_out), .Reset(Reset), .addr(pc_1_addr));
  Decode decode_1 (
    .instruction(mipsprogramrom_1_p2), .rt(decode_1_rt), .rs(decode_1_rs), .opcode(decode_1_opcode),
    .imm(decode_1_imm));  // open: funct, shamt, rd, addr
  // MIPSProgramROM mipsprogramrom_1: pin names not known; wires that end beside it: pc_1_addr, mipsprogramrom_1_p2
  // RegisterFile registerfile_1: pin names not known; wires that end beside it: registerfile_1_p1, CLK_out, registerfile_1_p3, decode_1_rt, decode_1_rs, registerfile_1_p6
  bit_extend bit_extend_1 (.imm(decode_1_imm), .ExOp(control_1_exop), .y(bit_extend_1_y));
  Control control_1 (
    .opcode(decode_1_opcode), .ALUOp(control_1_aluop), .RegWrite(registerfile_1_p3), .ExOp(control_1_exop),
    .SLTOp(control_1_sltop));
  // Mips_ALU mips_alu_1: pin names not known; wires that end beside it: registerfile_1_p6, bit_extend_1_y, control_1_aluop, mips_alu_1_p4
  assign bit_extender_1_out = {{31{1'b0}}, slt_1_y};  // Bit_Extender bit_extender_1
  slt slt_1 (.A(registerfile_1_p6), .B(bit_extend_1_y), .u(control_1_exop), .y(slt_1_y));
  Multiplexer #(.width(32), .enable("false")) multiplexer_1 (
    .in0(mips_alu_1_p4), .in1(bit_extender_1_out), .out(registerfile_1_p1), .sel(control_1_sltop));

  // Notes on the sheet:
  //   contents of mipsprogramrom_1 (hex, n*v repeats v):
  //   ADDIU $2, $zero, -10912 ADDIU $3, $zero, -16837 ADDIU $4, $zero, 24393  SLTIU $5, $1, -20799 SLTIU
  //   $6, $2, -10912 SLTIU $7, $3, -16837 SLTI $8, $4, 24393  SLTIU $5, $2, 10230 SLTI $6, $3, -8073 SLTIU
  //   $7, $2, 25708 SLTIU $8, $2, 9393 SLTIU $9, $1, 9388 SLTIU $10, $3, 9030 SLTI $11, $1, -13847 SLTIU
  //   $12, $3, 24515 SLTI $13, $3, 12504 SLTIU $14, $2, 6849 SLTIU $15, $3, -9869 SLTI $16, $2, -21317
  //   SLTI $17, $3, -13736 SLTIU $18, $2, 2119 SLTIU $19, $3, -26589 SLTI $20, $2, -27763 SLTIU $21, $1,
  //   -14958 SLTIU $22, $2, 3806 SLTI $23, $1, -29446 SLTIU $24, $3, -23798 SLTI $25, $3, 29416 SLTI $26,
  //   $2, 8412 SLTIU $27, $2, -14859 SLTI $28, $1, 21251 SLTI $29, $2, -635 SLTI $30, $2, 28461
endmodule

module slt (
  input  [31:0] A,
  input  [31:0] B,
  input  u,
  output y
);

  wire comparator_1_lt, comparator_2_lt;

  Comparator #(.width(16), .mode("unsigned")) comparator_1 (
    .a(A[15:0]), .b(B[15:0]), .lt(comparator_1_lt));  // open: gt, eq
  Comparator #(.width(16)) comparator_2 (.a(A[15:0]), .b(B[15:0]), .lt(comparator_2_lt));  // open: gt, eq
  Multiplexer #(.enable("false")) multiplexer_1 (.in0(comparator_1_lt), .in1(comparator_2_lt), .out(y), .sel(u));
endmodule
