// Logisim project main.circ as structural Verilog
module PC (
  input  clk,
  input  reset,
  input  [31:0] bta,
  input  [25:0] jaddr,
  input  jmpSrc,
  input  jmp,
  output [31:0] addr
);

  wire [3:0] bitselector_1_out;
  wire [31:0] adder_1_out, multiplexer_1_out, multiplexer_2_out;

  BitSelector #(.width(32), .group(4)) bitselector_1 (.in(addr), .out(bitselector_1_out), .sel(3'b111));
  Adder #(.width(32)) adder_1 (.a(addr), .b(32'h4), .out(adder_1_out));  // open: cin, cout
  Multiplexer #(.width(32), .enable("false")) multiplexer_1 (
    .in0(adder_1_out), .in1(multiplexer_2_out), .out(multiplexer_1_out), .sel(jmp));
  Multiplexer #(.width(32), .enable("false")) multiplexer_2 (
    .in0({bitselector_1_out, jaddr, 2'b00}), .in1(bta), .out(multiplexer_2_out), .sel(jmpSrc));
  Register #(.width(32)) register_1 (.D(multiplexer_1_out), .clk(clk), .Q(addr), .clr(reset));  // open: en
endmodule

module Decode (
  input  [31:0] instruction,
  output [15:0] imm,
  output [5:0] funct,
  output [4:0] shamt,
  output [4:0] rd,
  output [4:0] rt,
  output [4:0] rs,
  output [5:0] opcode,
  output [25:0] addr
);


  assign addr = instruction[25:0];
  assign funct = instruction[5:0];
  assign imm = instruction[15:0];
  assign opcode = instruction[31:26];
  assign rd = instruction[15:11];
  assign rs = instruction[25:21];
  assign rt = instruction[20:16];
  assign shamt = instruction[10:6];

  // Notes on the sheet:
  //   op addr
  //   imm / rd shamt funct
  //   op rs rt
endmodule

module op_alu (
  input  x5,
  input  x4,
  input  x3,
  input  x2,
  input  x1,
  input  x0,
  output a3,
  output a2,
  output a1,
  output a0
);

  wire and_1_out, and_2_out, and_3_out, and_4_out, and_5_out, and_6_out, and_7_out, and_8_out, not_1_out,
       not_2_out, not_3_out, not_4_out, not_5_out, not_6_out, not_7_out, not_8_out, not_9_out, not_10_out,
       not_11_out, not_12_out, not_13_out, not_14_out, not_15_out, not_16_out, not_17_out, not_18_out,
       not_19_out;

  not not_1 (not_1_out, x5);
  not not_2 (not_2_out, x4);
  not not_3 (not_3_out, x1);
  not not_4 (not_4_out, x5);
  not not_5 (not_5_out, x4);
  not not_6 (not_6_out, x0);
  not not_7 (not_7_out, x5);
  not not_8 (not_8_out, x4);
  not not_9 (not_9_out, x3);
  not not_10 (not_10_out, x5);
  not not_11 (not_11_out, x4);
  not not_12 (not_12_out, x0);
  not not_13 (not_13_out, x1);
  not not_14 (not_14_out, x3);
  not not_15 (not_15_out, x3);
  not not_16 (not_16_out, x2);
  not not_17 (not_17_out, x5);
  not not_18 (not_18_out, x4);
  not not_19 (not_19_out, x3);
  and and_1 (and_1_out, not_1_out, not_2_out, x3, x2, not_3_out);
  and and_2 (and_2_out, not_4_out, not_5_out, x3, x2, not_6_out);
  and and_3 (and_3_out, not_7_out, not_8_out, not_9_out, x2);
  and and_4 (and_4_out, not_10_out, not_11_out, x2, x1, not_12_out);
  and and_5 (and_5_out, not_13_out, x0);
  and and_6 (and_6_out, not_14_out, x1);
  and and_7 (and_7_out, not_15_out, x2);
  and and_8 (and_8_out, x3, not_16_out);
  and and_9 (a0, not_17_out, not_18_out, not_19_out, x2);
  or or_1 (a3, and_1_out, and_2_out);
  or or_2 (a2, and_3_out, and_4_out);
  or or_3 (a1, and_5_out, and_6_out, and_7_out, and_8_out, x4, x5);
endmodule

module op_regwrite (
  input  x5,
  input  x4,
  input  x3,
  input  x2,
  input  x1,
  input  x0,
  output RegWrtite,
  output ExOp,
  output SLTOp,
  output slt_u,
  output RegDst,
  output ALUSrc,
  output MOVOp,
  output SASrc,
  output LUIOp,
  output jmp,
  output jmpSrc,
  output JALOp
);

  wire and_1_out, and_2_out, and_3_out, and_4_out, and_5_out, and_6_out, and_7_out, and_8_out, and_9_out,
       and_10_out, and_11_out, and_12_out, and_13_out, and_14_out, and_16_out, and_17_out, and_18_out,
       and_19_out, and_20_out, and_22_out, and_23_out, not_1_out, not_2_out, not_3_out, not_4_out, not_5_out,
       not_6_out, not_7_out, not_8_out, not_9_out, not_10_out, not_11_out, not_12_out, not_13_out,
       not_14_out, not_15_out, not_16_out, not_17_out, not_18_out, not_19_out, not_20_out, not_21_out,
       not_22_out, not_23_out, not_24_out, not_25_out, not_26_out, not_27_out, not_28_out, not_29_out,
       not_30_out, not_31_out, not_32_out, not_33_out, not_34_out, not_35_out, not_36_out, not_37_out,
       not_38_out, not_39_out, not_40_out, not_41_out, not_42_out, not_43_out, not_44_out, not_45_out,
       not_46_out;

  not not_1 (not_1_out, x2);
  not not_2 (not_2_out, x1);
  not not_3 (not_3_out, x3);
  not not_4 (not_4_out, x2);
  not not_5 (not_5_out, x5);
  not not_6 (not_6_out, x3);
  not not_7 (not_7_out, x0);
  not not_8 (not_8_out, x5);
  not not_9 (not_9_out, x4);
  not not_10 (not_10_out, x3);
  not not_11 (not_11_out, x5);
  not not_12 (not_12_out, x4);
  not not_13 (not_13_out, x2);
  not not_14 (not_14_out, x4);
  not not_15 (not_15_out, x2);
  not not_16 (not_16_out, x0);
  not not_17 (not_17_out, x5);
  not not_18 (not_18_out, x2);
  not not_19 (not_19_out, x2);
  not not_20 (not_20_out, x1);
  not not_21 (not_21_out, x5);
  not not_22 (not_22_out, x5);
  not not_23 (not_23_out, x4);
  not not_24 (not_24_out, x3);
  not not_25 (not_25_out, x2);
  not not_26 (not_26_out, x1);
  not not_27 (not_27_out, x0);
  not not_28 (not_28_out, x5);
  not not_29 (not_29_out, x1);
  not not_30 (not_30_out, x0);
  not not_31 (not_31_out, x5);
  not not_32 (not_32_out, x4);
  not not_33 (not_33_out, x5);
  not not_34 (not_34_out, x4);
  not not_35 (not_35_out, x3);
  not not_36 (not_36_out, x5);
  not not_37 (not_37_out, x4);
  not not_38 (not_38_out, x3);
  not not_39 (not_39_out, x5);
  not not_40 (not_40_out, x4);
  not not_41 (not_41_out, x3);
  not not_42 (not_42_out, x5);
  not not_43 (not_43_out, x4);
  not not_44 (not_44_out, x3);
  not not_45 (not_45_out, x2);
  and and_1 (and_1_out, not_1_out, not_2_out);
  and and_2 (and_2_out, not_3_out, not_4_out, x0);
  and and_3 (and_3_out, not_5_out, x3);
  and and_4 (and_4_out, x5, not_6_out);
  and and_5 (and_5_out, x5, not_7_out);
  and and_6 (and_6_out, x5, x2);
  and and_7 (and_7_out, not_8_out, not_9_out, not_10_out);
  not not_46 (not_46_out, x2);
  and and_8 (and_8_out, not_11_out, not_12_out, x3, not_13_out, x1);
  and and_9 (and_9_out, not_14_out, x3, not_15_out, x1, not_16_out);
  and and_10 (and_10_out, not_17_out, not_18_out, x0);
  and and_11 (and_11_out, not_19_out, not_20_out, x0);
  and and_12 (and_12_out, not_21_out, x3, x0);
  and and_13 (and_13_out, x4, x0);
  and and_14 (and_14_out, x5, x2, x0);
  and and_15 (RegDst, not_22_out, not_23_out, not_24_out, not_25_out, not_26_out, not_27_out);
  and and_16 (and_16_out, not_28_out, x3);
  and and_17 (and_17_out, x3, not_29_out);
  and and_18 (and_18_out, x3, not_30_out);
  and and_19 (and_19_out, x3, x2);
  and and_20 (and_20_out, x4, x3);
  and and_21 (LUIOp, not_31_out, not_32_out, x3, x2, x1, x0);
  and and_22 (and_22_out, not_33_out, not_34_out, not_35_out, x1);
  and and_23 (and_23_out, not_36_out, not_37_out, not_38_out, x2);
  and and_24 (jmpSrc, not_39_out, not_40_out, not_41_out, x2);
  and and_25 (JALOp, not_42_out, not_43_out, not_44_out, not_45_out, x1, x0);
  or or_1 (RegWrtite, and_1_out, and_2_out, and_3_out, x4, and_4_out, and_5_out, and_6_out);
  or or_2 (ExOp, and_7_out, not_46_out);
  or or_3 (SLTOp, and_8_out, and_9_out);
  or or_4 (slt_u, and_10_out, and_11_out, and_12_out, and_13_out, and_14_out);
  or or_5 (ALUSrc, and_16_out, and_17_out, and_18_out, and_19_out, and_20_out);
  or or_6 (jmp, and_22_out, and_23_out);

  assign MOVOp = 1'b0;
  assign SASrc = 1'b0;
endmodule

module op_branch (
  input  x5,
  input  x4,
  input  x3,
  input  x2,
  input  x1,
  input  x0,
  output branch,
  output branch1,
  output branch0
);

  wire not_1_out, not_2_out, not_3_out;

  not not_1 (not_1_out, x5);
  not not_2 (not_2_out, x4);
  not not_3 (not_3_out, x3);
  and and_1 (branch, not_1_out, not_2_out, not_3_out, x2);

  assign branch0 = x0;
  assign branch1 = x1;
endmodule

module op_mem (
  input  x5,
  input  x4,
  input  x3,
  input  x2,
  input  x1,
  input  x0,
  output MEMOp,
  output mem_u
);

  wire not_1_out, not_2_out, not_3_out, not_4_out;

  not not_1 (not_1_out, x4);
  not not_2 (not_2_out, x2);
  not not_3 (not_3_out, x4);
  not not_4 (not_4_out, x2);
  and and_1 (MEMOp, x5, not_1_out, not_2_out, x1, x0);
  and and_2 (mem_u, x5, not_3_out, x3, not_4_out, x1, x0);
endmodule

module funct_alu (
  input  x5,
  input  x4,
  input  x3,
  input  x2,
  input  x1,
  input  x0,
  output a3,
  output a2,
  output a1,
  output a0
);

  wire and_1_out, and_2_out, and_3_out, and_4_out, and_5_out, and_6_out, and_7_out, and_8_out, not_1_out,
       not_2_out, not_3_out, not_4_out, not_5_out, not_6_out;

  not not_1 (not_1_out, x1);
  not not_2 (not_2_out, x1);
  not not_3 (not_3_out, x5);
  not not_4 (not_4_out, x4);
  not not_5 (not_5_out, x3);
  not not_6 (not_6_out, x2);
  and and_1 (and_1_out, x2, not_1_out, x0);
  and and_2 (and_2_out, x3, x2);
  and and_3 (and_3_out, x4, x2);
  and and_4 (and_4_out, x5, x2);
  and and_5 (and_5_out, not_2_out, x0);
  and and_6 (and_6_out, x3, x0);
  and and_7 (and_7_out, x4, x0);
  and and_8 (and_8_out, x5, x0);
  and and_9 (a0, not_3_out, not_4_out, not_5_out, not_6_out, x1, x0);
  or or_1 (a3, and_1_out, and_2_out, and_3_out, and_4_out);
  or or_2 (a1, and_5_out, and_6_out, and_7_out, and_8_out);

  assign a2 = x1;
endmodule

module funct_regwrite (
  input  x5,
  input  x4,
  input  x3,
  input  x2,
  input  x1,
  input  x0,
  output SLTOp,
  output slt_u,
  output MOVOp,
  output mov_u,
  output SASrc,
  output jmp,
  output jmpSrc,
  output JALOp
);

  wire and_1_out, and_2_out, and_3_out, and_4_out, and_5_out, and_6_out, and_7_out, and_8_out, and_9_out,
       and_11_out, and_12_out, and_13_out, and_14_out, and_15_out, not_1_out, not_2_out, not_3_out,
       not_4_out, not_5_out, not_6_out, not_7_out, not_8_out, not_9_out, not_10_out, not_11_out, not_12_out,
       not_13_out, not_14_out, not_15_out, not_16_out, not_17_out;

  and and_1 (and_1_out, x3, x1);
  and and_2 (and_2_out, x3, x2);
  and and_3 (and_3_out, x4, x3);
  and and_4 (and_4_out, x5, x3);
  not not_1 (not_1_out, x3);
  not not_2 (not_2_out, x5);
  not not_3 (not_3_out, x4);
  not not_4 (not_4_out, x2);
  not not_5 (not_5_out, x3);
  not not_6 (not_6_out, x5);
  not not_7 (not_7_out, x4);
  not not_8 (not_8_out, x2);
  not not_9 (not_9_out, x1);
  not not_10 (not_10_out, x5);
  not not_11 (not_11_out, x4);
  not not_12 (not_12_out, x2);
  not not_13 (not_13_out, x1);
  not not_14 (not_14_out, x5);
  not not_15 (not_15_out, x4);
  not not_16 (not_16_out, x2);
  not not_17 (not_17_out, x1);
  or or_1 (SLTOp, and_1_out, and_2_out, and_3_out, and_4_out);
  and and_5 (and_5_out, not_1_out, x0);
  and and_6 (and_6_out, x1, x0);
  and and_7 (and_7_out, x2, x0);
  and and_8 (and_8_out, x4, x0);
  and and_9 (and_9_out, x5, x0);
  and and_10 (MOVOp, not_2_out, not_3_out, x3, not_4_out, x1);
  and and_11 (and_11_out, not_5_out, x0);
  and and_12 (and_12_out, x1, x0);
  and and_13 (and_13_out, x2, x0);
  and and_14 (and_14_out, x4, x0);
  and and_15 (and_15_out, x5, x0);
  and and_16 (jmp, not_6_out, not_7_out, x3, not_8_out, not_9_out);
  and and_17 (jmpSrc, not_10_out, not_11_out, x3, not_12_out, not_13_out);
  and and_18 (JALOp, not_14_out, not_15_out, x3, not_16_out, not_17_out, x0);
  or or_2 (slt_u, and_5_out, and_6_out, and_7_out, and_8_out, and_9_out);
  or or_3 (mov_u, and_11_out, and_12_out, and_13_out, and_14_out, and_15_out);

  assign SASrc = x2;
endmodule

module Control (
  input  [5:0] opcode,
  input  [5:0] funct,
  output [3:0] ALUOp,
  output RegWrite,
  output ExOp,
  output SLTOp,
  output slt_u,
  output RegDst,
  output ALUSrc,
  output MOVOp,
  output mov_u,
  output SASrc,
  output LUIOp,
  output jmp,
  output jmpSrc,
  output JALOp,
  output branch,
  output [1:0] branchOp,
  output MEMOp,
  output mem_u
);

  wire funct_regwrite_1_jalop, funct_regwrite_1_jmp, funct_regwrite_1_jmpsrc, funct_regwrite_1_movop,
       funct_regwrite_1_sasrc, funct_regwrite_1_slt_u, funct_regwrite_1_sltop, nor_1_out,
       op_regwrite_1_jalop, op_regwrite_1_jmp, op_regwrite_1_jmpsrc, op_regwrite_1_movop,
       op_regwrite_1_sasrc, op_regwrite_1_slt_u, op_regwrite_1_sltop;
  wire [3:0] funct_alu_1_a0, op_alu_1_a0;

  nor nor_1 (nor_1_out, opcode[5], opcode[4], opcode[3], opcode[2], opcode[1], opcode[0]);
  op_alu op_alu_1 (
    .x5(opcode[5]), .x4(opcode[4]), .x3(opcode[3]), .x2(opcode[2]), .x1(opcode[1]), .x0(opcode[0]),
    .a3(op_alu_1_a0[3]), .a2(op_alu_1_a0[2]), .a1(op_alu_1_a0[1]), .a0(op_alu_1_a0[0]));
  op_regwrite op_regwrite_1 (
    .x5(opcode[5]), .x4(opcode[4]), .x3(opcode[3]), .x2(opcode[2]), .x1(opcode[1]), .x0(opcode[0]),
    .RegWrtite(RegWrite), .ExOp(ExOp), .SLTOp(op_regwrite_1_sltop), .slt_u(op_regwrite_1_slt_u),
    .RegDst(RegDst), .ALUSrc(ALUSrc), .MOVOp(op_regwrite_1_movop), .SASrc(op_regwrite_1_sasrc),
    .LUIOp(LUIOp), .jmp(op_regwrite_1_jmp), .jmpSrc(op_regwrite_1_jmpsrc), .JALOp(op_regwrite_1_jalop));
  op_branch op_branch_1 (
    .x5(opcode[5]), .x4(opcode[4]), .x3(opcode[3]), .x2(opcode[2]), .x1(opcode[1]), .x0(opcode[0]),
    .branch(branch), .branch1(branchOp[1]), .branch0(branchOp[0]));
  op_mem op_mem_1 (
    .x5(opcode[5]), .x4(opcode[4]), .x3(opcode[3]), .x2(opcode[2]), .x1(opcode[1]), .x0(opcode[0]),
    .MEMOp(MEMOp), .mem_u(mem_u));
  funct_alu funct_alu_1 (
    .x5(funct[5]), .x4(funct[4]), .x3(funct[3]), .x2(funct[2]), .x1(funct[1]), .x0(funct[0]),
    .a3(funct_alu_1_a0[3]), .a2(funct_alu_1_a0[2]), .a1(funct_alu_1_a0[1]), .a0(funct_alu_1_a0[0]));
  funct_regwrite funct_regwrite_1 (
    .x5(funct[5]), .x4(funct[4]), .x3(funct[3]), .x2(funct[2]), .x1(funct[1]), .x0(funct[0]),
    .SLTOp(funct_regwrite_1_sltop), .slt_u(funct_regwrite_1_slt_u), .MOVOp(funct_regwrite_1_movop),
    .mov_u(mov_u), .SASrc(funct_regwrite_1_sasrc), .jmp(funct_regwrite_1_jmp),
    .jmpSrc(funct_regwrite_1_jmpsrc), .JALOp(funct_regwrite_1_jalop));
  Multiplexer #(.enable("false")) multiplexer_1 (
    .in0(op_regwrite_1_jalop), .in1(funct_regwrite_1_jalop), .out(JALOp), .sel(nor_1_out));
  Multiplexer #(.width(4), .enable("false")) multiplexer_2 (
    .in0(op_alu_1_a0), .in1(funct_alu_1_a0), .out(ALUOp), .sel(nor_1_out));
  Multiplexer #(.enable("false")) multiplexer_3 (
    .in0(op_regwrite_1_sltop), .in1(funct_regwrite_1_sltop), .out(SLTOp), .sel(nor_1_out));
  Multiplexer #(.enable("false")) multiplexer_4 (
    .in0(op_regwrite_1_slt_u), .in1(funct_regwrite_1_slt_u), .out(slt_u), .sel(nor_1_out));
  Multiplexer #(.enable("false")) multiplexer_5 (
    .in0(op_regwrite_1_movop), .in1(funct_regwrite_1_movop), .out(MOVOp), .sel(nor_1_out));
  Multiplexer #(.enable("false")) multiplexer_6 (
    .in0(op_regwrite_1_sasrc), .in1(funct_regwrite_1_sasrc), .out(SASrc), .sel(nor_1_out));
  Multiplexer #(.enable("false")) multiplexer_7 (
    .in0(op_regwrite_1_jmp), .in1(funct_regwrite_1_jmp), .out(jmp), .sel(nor_1_out));
  Multiplexer #(.enable("false")) multiplexer_8 (
    .in0(op_regwrite_1_jmpsrc), .in1(funct_regwrite_1_jmpsrc), .out(jmpSrc), .sel(nor_1_out));
endmodule

module BitExtend (
  input  [15:0] imm,
  input  ExOp,
  output [31:0] y
);

  wire [31:0] bit_extender_1_out, bit_extender_2_out;

  assign bit_extender_1_out = {{16{1'b0}}, imm};  // Bit_Extender bit_extender_1
  assign bit_extender_2_out = {{16{imm[15]}}, imm};  // Bit_Extender bit_extender_2
  Multiplexer #(.width(32), .enable("false")) multiplexer_1 (
    .in0(bit_extender_1_out), .in1(bit_extender_2_out), .out(y), .sel(ExOp));
endmodule

module slt (
  input  [31:0] A,
  input  [31:0] B,
  input  slt_u,
  output [31:0] y
);

  wire comparator_1_lt, comparator_2_lt, multiplexer_1_out;

  Comparator #(.width(32)) comparator_1 (.a(A), .b(B), .lt(comparator_1_lt));  // open: gt, eq
  Comparator #(.width(32), .mode("unsigned")) comparator_2 (.a(A), .b(B), .lt(comparator_2_lt));  // open: gt, eq
  Multiplexer #(.enable("false")) multiplexer_1 (
    .in0(comparator_1_lt), .in1(comparator_2_lt), .out(multiplexer_1_out), .sel(slt_u));
  assign y = {{31{1'b0}}, multiplexer_1_out};  // Bit_Extender bit_extender_1
endmodule

module tsk5_1 (
  input  reset
);

  wire clock_1_out, control_1_exop, control_1_slt_u, control_1_sltop, registerfile_1_p2;
  wire [3:0] control_1_aluop;
  wire [4:0] decode_1_rs, decode_1_rt;
  wire [5:0] decode_1_opcode;
  wire [15:0] decode_1_imm;
  wire [31:0] bitextend_1_y, mips_alu_1_p4, mipsprogramrom_1_p2, pc_1_addr, registerfile_1_p1,
       registerfile_1_p5, slt_1_y;

  Clock clock_1 (.out(clock_1_out));
  PC pc_1 (.reset(reset), .clk(clock_1_out), .addr(pc_1_addr));  // open: bta, jmp, jaddr, jmpSrc
  // MIPSProgramROM mipsprogramrom_1: pin names not known; wires that end beside it: pc_1_addr, mipsprogramrom_1_p2, clock_1_out
  Decode decode_1 (
    .rs(decode_1_rs), .instruction(mipsprogramrom_1_p2), .imm(decode_1_imm), .rt(decode_1_rt),
    .opcode(decode_1_opcode));  // open: rd, funct, shamt, addr
  // RegisterFile registerfile_1: pin names not known; wires that end beside it: registerfile_1_p1, registerfile_1_p2, decode_1_rt, decode_1_rs, registerfile_1_p5
  Control control_1 (
    .slt_u(control_1_slt_u), .ALUOp(control_1_aluop), .RegWrite(registerfile_1_p2), .SLTOp(control_1_sltop),
    .opcode(decode_1_opcode), .ExOp(control_1_exop));  // open: mov_u, SASrc, RegDst, jmpSrc, jmp, LUIOp, MOVOp, funct, ALUSrc, JALOp, branch, branchOp, MEMOp, mem_u
  BitExtend bitextend_1 (.imm(decode_1_imm), .ExOp(control_1_exop), .y(bitextend_1_y));
  slt slt_1 (.A(registerfile_1_p5), .B(bitextend_1_y), .slt_u(control_1_slt_u), .y(slt_1_y));
  // Mips_ALU mips_alu_1: pin names not known; wires that end beside it: registerfile_1_p5, bitextend_1_y, control_1_aluop, mips_alu_1_p4
  Multiplexer #(.width(32), .enable("false")) multiplexer_1 (
    .in0(mips_alu_1_p4), .in1(slt_1_y), .out(registerfile_1_p1), .sel(control_1_sltop));

  // Notes on the sheet:
  //   contents of mipsprogramrom_1 (hex, n*v repeats v):
  //   addiu $2, $0, 1 addiu $3, $0, 0x7ff0 addiu $4, $0, 0x5000  andi $5, $1, 0x5555   andi $6, $1, 0xaaaa
  //   ori $7, $2, 0xaaa0    xori $8, $2, 0xaaaa
endmodule

module mov (
  input  [31:0] rt,
  input  mov_u,
  output WE
);

  wire comparator_1_eq;

  Comparator #(.width(32)) comparator_1 (.a(rt), .b({32{1'b0}}), .eq(comparator_1_eq));  // open: gt, lt
  xor xor_1 (WE, comparator_1_eq, mov_u);
endmodule

module SA (
  input  [4:0] shamt,
  input  [31:0] rs,
  input  SAsrc,
  input  LUIOp,
  output [4:0] SA
);

  wire [4:0] bitselector_1_out, multiplexer_1_out;

  BitSelector #(.width(32), .group(5)) bitselector_1 (.in(rs), .out(bitselector_1_out), .sel(3'b000));
  Multiplexer #(.width(5), .enable("false")) multiplexer_1 (
    .in0(shamt), .in1(bitselector_1_out), .out(multiplexer_1_out), .sel(SAsrc));
  Multiplexer #(.width(5), .enable("false")) multiplexer_2 (
    .in0(multiplexer_1_out), .in1(5'b10000), .out(SA), .sel(LUIOp));
endmodule

module tsk5_2 (
  input  reset
);

  wire clock_1_out, control_1_alusrc, control_1_exop, control_1_luiop, control_1_mov_u, control_1_movop,
       control_1_regdst, control_1_regwrite, control_1_sasrc, control_1_slt_u, control_1_sltop, mov_1_we,
       multiplexer_2_out, not_1_out;
  wire [3:0] control_1_aluop;
  wire [4:0] decode_1_rd, decode_1_rs, decode_1_rt, decode_1_shamt, multiplexer_1_out, sa_1_sa;
  wire [5:0] decode_1_funct, decode_1_opcode;
  wire [15:0] decode_1_imm;
  wire [25:0] decode_1_addr;
  wire [31:0] bitextend_1_y, mips_alu_1_p5, mipsprogramrom_1_p2, mipsprogramrom_1_p4, multiplexer_3_out,
       multiplexer_4_out, pc_1_addr, registerfile_1_p5, registerfile_1_p6, slt_1_y;

  Clock clock_1 (.out(clock_1_out));
  PC pc_1 (.reset(reset), .clk(clock_1_out), .addr(pc_1_addr));  // open: bta, jmp, jaddr, jmpSrc
  Control control_1 (
    .mov_u(control_1_mov_u), .slt_u(control_1_slt_u), .ALUOp(control_1_aluop), .SASrc(control_1_sasrc),
    .RegWrite(control_1_regwrite), .RegDst(control_1_regdst), .LUIOp(control_1_luiop),
    .MOVOp(control_1_movop), .SLTOp(control_1_sltop), .funct(decode_1_funct), .opcode(decode_1_opcode),
    .ExOp(control_1_exop), .ALUSrc(control_1_alusrc));  // open: jmpSrc, jmp, JALOp, branch, branchOp, MEMOp, mem_u
  Decode decode_1 (
    .rs(decode_1_rs), .rd(decode_1_rd), .funct(decode_1_funct), .instruction(mipsprogramrom_1_p2),
    .imm(decode_1_imm), .shamt(decode_1_shamt), .rt(decode_1_rt), .opcode(decode_1_opcode),
    .addr(decode_1_addr));
  // MIPSProgramROM mipsprogramrom_1: pin names not known; wires that end beside it: pc_1_addr, mipsprogramrom_1_p2, decode_1_addr, mipsprogramrom_1_p4, clock_1_out
  Multiplexer #(.width(5), .enable("false")) multiplexer_1 (
    .in0(decode_1_rt), .in1(decode_1_rd), .out(multiplexer_1_out), .sel(control_1_regdst));
  Multiplexer #(.enable("false")) multiplexer_2 (
    .in0(control_1_regwrite), .in1(mov_1_we), .out(multiplexer_2_out), .sel(control_1_movop));
  BitExtend bitextend_1 (.imm(decode_1_imm), .ExOp(control_1_exop), .y(bitextend_1_y));
  // RegisterFile registerfile_1: pin names not known; wires that end beside it: multiplexer_2_out, multiplexer_1_out, decode_1_rs, decode_1_rt, registerfile_1_p5, registerfile_1_p6
  Multiplexer #(.width(32), .enable("false")) multiplexer_3 (
    .in0(registerfile_1_p6), .in1(bitextend_1_y), .out(multiplexer_3_out), .sel(control_1_alusrc));
  mov mov_1 (.rt(registerfile_1_p6), .mov_u(control_1_mov_u), .WE(mov_1_we));
  SA sa_1 (
    .shamt(decode_1_shamt), .rs(registerfile_1_p5), .SAsrc(control_1_sasrc), .LUIOp(control_1_luiop),
    .SA(sa_1_sa));
  slt slt_1 (.A(registerfile_1_p5), .B(multiplexer_3_out), .slt_u(control_1_slt_u), .y(slt_1_y));
  // Mips_ALU mips_alu_1: pin names not known; wires that end beside it: registerfile_1_p5, multiplexer_3_out, control_1_aluop, sa_1_sa, mips_alu_1_p5
  Multiplexer #(.width(32), .enable("false")) multiplexer_4 (
    .in0(mips_alu_1_p5), .in1(slt_1_y), .out(multiplexer_4_out), .sel(control_1_sltop));
  not not_1 (not_1_out, control_1_movop);
  Multiplexer #(.width(32), .enable("false")) multiplexer_5 (
    .in0(registerfile_1_p5), .in1(multiplexer_4_out), .out(mipsprogramrom_1_p4), .sel(not_1_out));

  // Notes on the sheet:
  //   contents of mipsprogramrom_1 (hex, n*v repeats v):
  //   LUI $1, 33848 LUI $2, 74 LUI $3, 56045 LUI $4, 27330 LUI $5, 15254 LUI $6, 37593 LUI $7, 15517 LUI
  //   $8, 6457 LUI $9, 27493 LUI $10, 65378 LUI $11, 39311 LUI $12, 3604 LUI $13, 65518 LUI $14, 1988 LUI
  //   $15, 57851 LUI $16, 34065 LUI $17, 56700 LUI $18, 36303 LUI $19, 56033 LUI $20, 47686 LUI $21, 44708
  //   LUI $22, 17702 LUI $23, 9308 LUI $24, 21814 LUI $25, 49082 LUI $26, 27503 LUI $27, 25174 LUI $28,
  //   65475 LUI $29, 39676 LUI $30, 6595 LUI $31, 33220 ORI $4, $4, 0xbeef ORI $5, $5, 0xd00d ORI $6, $6,
  //   0xabba ORI $7, $7, 0xc0de ORI $8, $8, 0xbeef ORI $9, $9, 0xface ORI $10, $10, 0xdec0 ORI $11, $11,
  //   0xfe0d
  //   rs
  //   RegDst
  //   rd
  //   MOVOp
  //   rt
  //   ALUSrc
  //   SLTOp
  //   ~MOVOp
endmodule

module zero (
  input  [31:0] C,
  output zero,
  output neg
);

  BitSelector #(.width(32)) bitselector_1 (.in(C), .out(neg), .sel({5{1'b1}}));
  nor nor_1 (zero, C[0], C[1], C[2], C[3], C[4], C[5], C[6], C[7], C[8], C[9], C[10], C[11], C[12], C[13], C[14], C[15], C[16], C[17], C[18], C[19], C[20], C[21], C[22], C[23], C[24], C[25], C[26], C[27], C[28], C[29], C[30], C[31]);
endmodule

module BTA (
  input  [31:0] imm_ext,
  input  [31:0] PC_plus_4,
  output [31:0] BTA
);

  wire [31:0] shifter_1_out;

  Shifter #(.width(32)) shifter_1 (.in(imm_ext), .\dist (5'b00010), .out(shifter_1_out));
  Adder #(.width(32)) adder_1 (.a(shifter_1_out), .b(PC_plus_4), .out(BTA));  // open: cin, cout
endmodule

module BTA_sel (
  input  zero,
  input  neg,
  input  [1:0] branchOp,
  output BTA_u
);

  wire not_1_out, not_2_out, or_1_out;

  not not_1 (not_1_out, zero);
  or or_1 (or_1_out, zero, neg);
  not not_2 (not_2_out, or_1_out);
  Multiplexer #(.select(2), .enable("false")) multiplexer_1 (
    .in0(zero), .in1(not_1_out), .in2(or_1_out), .in3(not_2_out), .out(BTA_u), .sel(branchOp));
endmodule

module tsk6 (
  input  reset
);

  wire and_1_out, bta_sel_1_bta_u, clock_1_out, control_1_alusrc, control_1_branch, control_1_exop,
       control_1_jalop, control_1_jmp, control_1_jmpsrc, control_1_luiop, control_1_mem_u, control_1_memop,
       control_1_mov_u, control_1_movop, control_1_regdst, control_1_regwrite, control_1_sasrc,
       control_1_slt_u, control_1_sltop, mov_1_we, multiplexer_5_out, not_1_out, not_2_out, not_3_out,
       not_4_out, zero_1_neg, zero_1_zero;
  wire [1:0] control_1_branchop;
  wire [3:0] control_1_aluop;
  wire [4:0] decode_1_rd, decode_1_rs, decode_1_rt, decode_1_shamt, multiplexer_3_out, multiplexer_6_out,
       sa_1_sa;
  wire [5:0] decode_1_funct, decode_1_opcode;
  wire [15:0] decode_1_imm;
  wire [23:0] bitselector_1_out;
  wire [25:0] decode_1_addr;
  wire [31:0] adder_1_out, adder_2_out, bitextend_1_y, bta_1_bta, mips_alu_1_p5, mips_ram_1_p6,
       mipsprogramrom_1_p2, multiplexer_1_out, multiplexer_2_out, multiplexer_4_out, multiplexer_7_out,
       multiplexer_8_out, multiplexer_9_out, multiplexer_10_out, pc_1_addr, registerfile_1_p7,
       registerfile_1_p8, slt_1_y;

  Clock clock_1 (.out(clock_1_out));
  PC pc_1 (
    .bta(multiplexer_1_out), .reset(reset), .jmp(control_1_jmp), .jaddr(decode_1_addr), .clk(clock_1_out),
    .jmpSrc(control_1_jmpsrc), .addr(pc_1_addr));
  Multiplexer #(.width(32), .enable("false")) multiplexer_1 (
    .in0(multiplexer_2_out), .in1(registerfile_1_p7), .out(multiplexer_1_out), .sel(not_1_out));
  not not_1 (not_1_out, control_1_branch);
  Decode decode_1 (
    .rs(decode_1_rs), .rd(decode_1_rd), .funct(decode_1_funct), .instruction(mipsprogramrom_1_p2),
    .imm(decode_1_imm), .shamt(decode_1_shamt), .rt(decode_1_rt), .opcode(decode_1_opcode),
    .addr(decode_1_addr));
  // MIPSProgramROM mipsprogramrom_1: pin names not known; wires that end beside it: pc_1_addr, mipsprogramrom_1_p2
  Adder #(.width(32)) adder_1 (.a(pc_1_addr), .b(32'h4), .out(adder_1_out));  // open: cin, cout
  Multiplexer #(.width(32), .enable("false")) multiplexer_2 (
    .in0(adder_1_out), .in1(bta_1_bta), .out(multiplexer_2_out), .sel(bta_sel_1_bta_u));
  Control control_1 (
    .mov_u(control_1_mov_u), .slt_u(control_1_slt_u), .ALUOp(control_1_aluop), .SASrc(control_1_sasrc),
    .RegWrite(control_1_regwrite), .RegDst(control_1_regdst), .jmpSrc(control_1_jmpsrc), .jmp(control_1_jmp),
    .LUIOp(control_1_luiop), .MOVOp(control_1_movop), .SLTOp(control_1_sltop), .funct(decode_1_funct),
    .opcode(decode_1_opcode), .ExOp(control_1_exop), .ALUSrc(control_1_alusrc), .JALOp(control_1_jalop),
    .branch(control_1_branch), .branchOp(control_1_branchop), .MEMOp(control_1_memop), .mem_u(control_1_mem_u));
  and and_1 (and_1_out, control_1_memop, control_1_mem_u);
  BTA bta_1 (.BTA(bta_1_bta), .imm_ext(bitextend_1_y), .PC_plus_4(adder_1_out));
  Multiplexer #(.width(5), .enable("false")) multiplexer_3 (
    .in0(decode_1_rt), .in1({5{1'b1}}), .out(multiplexer_3_out), .sel(control_1_jalop));
  Multiplexer #(.width(32), .enable("false")) multiplexer_4 (
    .in0(multiplexer_9_out), .in1(adder_1_out), .out(multiplexer_4_out), .sel(control_1_jalop));
  Multiplexer #(.enable("false")) multiplexer_5 (
    .in0(control_1_regwrite), .in1(mov_1_we), .out(multiplexer_5_out), .sel(control_1_movop));
  BitExtend bitextend_1 (.imm(decode_1_imm), .ExOp(control_1_exop), .y(bitextend_1_y));
  Multiplexer #(.width(5), .enable("false")) multiplexer_6 (
    .in0(multiplexer_3_out), .in1(decode_1_rd), .out(multiplexer_6_out), .sel(control_1_regdst));
  // RegisterFile registerfile_1: pin names not known; wires that end beside it: multiplexer_4_out, clock_1_out, multiplexer_5_out, multiplexer_6_out, decode_1_rs, decode_1_rt, registerfile_1_p7, registerfile_1_p8
  Multiplexer #(.width(32), .enable("false")) multiplexer_7 (
    .in0(registerfile_1_p8), .in1(bitextend_1_y), .out(multiplexer_7_out), .sel(control_1_alusrc));
  Adder #(.width(32)) adder_2 (.a(registerfile_1_p7), .b(bitextend_1_y), .out(adder_2_out));  // open: cin, cout
  mov mov_1 (.rt(registerfile_1_p8), .mov_u(control_1_mov_u), .WE(mov_1_we));
  SA sa_1 (
    .shamt(decode_1_shamt), .rs(registerfile_1_p7), .SAsrc(control_1_sasrc), .LUIOp(control_1_luiop),
    .SA(sa_1_sa));
  BitSelector #(.width(32), .group(24)) bitselector_1 (.in(adder_2_out), .out(bitselector_1_out), .sel(1'b0));
  slt slt_1 (.A(registerfile_1_p7), .B(multiplexer_7_out), .slt_u(control_1_slt_u), .y(slt_1_y));
  // Mips_ALU mips_alu_1: pin names not known; wires that end beside it: registerfile_1_p7, multiplexer_7_out, control_1_aluop, sa_1_sa, mips_alu_1_p5
  not not_2 (not_2_out, and_1_out);
  Multiplexer #(.width(32), .enable("false")) multiplexer_8 (
    .in0(mips_alu_1_p5), .in1(slt_1_y), .out(multiplexer_8_out), .sel(control_1_sltop));
  zero zero_1 (.C(mips_alu_1_p5), .zero(zero_1_zero), .neg(zero_1_neg));
  // MIPS_RAM #(.addrWidth(24)) mips_ram_1: pin names not known; wires that end beside it: bitselector_1_out, registerfile_1_p8, and_1_out, clock_1_out, not_2_out, mips_ram_1_p6
  Multiplexer #(.width(32), .enable("false")) multiplexer_9 (
    .in0(mips_ram_1_p6), .in1(multiplexer_10_out), .out(multiplexer_9_out), .sel(not_4_out));
  BTA_sel bta_sel_1 (.BTA_u(bta_sel_1_bta_u), .neg(zero_1_neg), .branchOp(control_1_branchop), .zero(zero_1_zero));
  not not_3 (not_3_out, control_1_movop);
  Multiplexer #(.width(32), .enable("false")) multiplexer_10 (
    .in0(registerfile_1_p7), .in1(multiplexer_8_out), .out(multiplexer_10_out), .sel(not_3_out));
  not not_4 (not_4_out, control_1_memop);

  // Notes on the sheet:
  //   ~branch
  //   zero & branch
  //   contents of mipsprogramrom_1 (hex, n*v repeats v):
  //   addiu $2, $0, 0x000c  sw $1, 0($2) lw $3, 0($2)  addiu $0, $0, 0
  //   JALOp
  //   JALOp
  //   rs
  //   rt
  //   RegDst
  //   rd
  //   MOVOp
  //   ALUSrc
  //   MEMOp & mem_u
  //   SLTOp
  //   ~MOVOp
  //   ~MEMOp
endmodule
