// Logisim project moore_mealy.circ as structural Verilog
module moore1_next (
  input  ps1,
  input  ps2,
  input  ps3,
  input  i,
  output ns1,
  output ns2,
  output ns3
);

  wire and_2_out, and_3_out, and_4_out, and_5_out, and_6_out, and_7_out, not_1_out, not_2_out, not_3_out,
       not_4_out, not_5_out, not_6_out;

  and and_1 (ns1, ps2, ps3, i);
  not not_1 (not_1_out, ps2);
  and and_2 (and_2_out, not_1_out, ps3, not_2_out);
  not not_2 (not_2_out, i);
  not not_3 (not_3_out, ps3);
  and and_3 (and_3_out, ps2, not_3_out, not_4_out);
  not not_4 (not_4_out, i);
  and and_4 (and_4_out, ps1, ps2);
  not not_5 (not_5_out, ps2);
  and and_5 (and_5_out, not_5_out, i);
  and and_6 (and_6_out, ps2, not_6_out);
  not not_6 (not_6_out, ps3);
  and and_7 (and_7_out, ps1, ps2);
  or or_1 (ns2, and_2_out, and_3_out, and_4_out);
  or or_2 (ns3, and_5_out, and_6_out, and_7_out);
endmodule

module moore1_out (
  input  ps1,
  input  ps2,
  input  ps3,
  output o
);


  assign o = ps1;
endmodule

module moore1 (
  input  i,
  output o
);

  wire clock_1_out, d_ff_1_q, d_ff_2_q, d_ff_3_q, moore1_next_1_ns1, moore1_next_1_ns2, moore1_next_1_ns3;

  moore1_next moore1_next_1 (
    .ps1(d_ff_1_q), .ps2(d_ff_2_q), .ps3(d_ff_3_q), .i(i), .ns1(moore1_next_1_ns1), .ns2(moore1_next_1_ns2),
    .ns3(moore1_next_1_ns3));
  Clock clock_1 (.out(clock_1_out));
  D_Flip_Flop d_ff_1 (.D(moore1_next_1_ns1), .clk(clock_1_out), .Q(d_ff_1_q));  // open: Qn, preset, reset
  D_Flip_Flop d_ff_2 (.D(moore1_next_1_ns2), .clk(clock_1_out), .Q(d_ff_2_q));  // open: Qn, preset, reset
  D_Flip_Flop d_ff_3 (.D(moore1_next_1_ns3), .clk(clock_1_out), .Q(d_ff_3_q));  // open: Qn, preset, reset
  moore1_out moore1_out_1 (.ps1(d_ff_1_q), .ps2(d_ff_2_q), .ps3(d_ff_3_q), .o(o));
endmodule

module moore2_next (
  input  ps1,
  input  ps2,
  input  ps3,
  input  ps4,
  input  ps5,
  input  i,
  output ns1,
  output ns2,
  output ns3,
  output ns4,
  output ns5
);

  wire and_5_out, and_6_out, not_1_out, not_2_out, not_3_out, not_4_out, not_5_out, not_6_out, not_7_out,
       not_8_out;

  and and_1 (ns1, ps2, i);
  not not_1 (not_1_out, i);
  not not_2 (not_2_out, i);
  not not_3 (not_3_out, ps2);
  not not_4 (not_4_out, i);
  not not_5 (not_5_out, ps2);
  not not_6 (not_6_out, ps3);
  not not_7 (not_7_out, ps4);
  not not_8 (not_8_out, i);
  and and_2 (ns2, ps3, not_1_out);
  and and_3 (ns3, ps4, not_2_out);
  and and_4 (ns4, not_3_out, i);
  and and_5 (and_5_out, ps5, not_4_out);
  and and_6 (and_6_out, ps1, not_5_out, not_6_out, not_7_out, not_8_out);
  or or_1 (ns5, and_5_out, and_6_out);
endmodule

module moore2_out (
  input  ps1,
  input  ps2,
  input  ps3,
  input  ps4,
  input  ps5,
  output out
);


  assign out = ps1;
endmodule

module moore2 (
  input  i,
  output o
);

  wire clock_1_out, d_ff_1_q, d_ff_2_q, d_ff_3_q, d_ff_4_q, d_ff_5_q, moore2_next_1_ns1, moore2_next_1_ns2,
       moore2_next_1_ns3, moore2_next_1_ns4, moore2_next_1_ns5;

  moore2_next moore2_next_1 (
    .ps1(d_ff_1_q), .ps2(d_ff_2_q), .ps3(d_ff_3_q), .ps4(d_ff_4_q), .ps5(d_ff_5_q), .i(i),
    .ns1(moore2_next_1_ns1), .ns2(moore2_next_1_ns2), .ns3(moore2_next_1_ns3), .ns4(moore2_next_1_ns4),
    .ns5(moore2_next_1_ns5));
  D_Flip_Flop d_ff_1 (.D(moore2_next_1_ns1), .clk(clock_1_out), .Q(d_ff_1_q));  // open: Qn, preset, reset
  D_Flip_Flop d_ff_2 (.D(moore2_next_1_ns2), .clk(clock_1_out), .Q(d_ff_2_q));  // open: Qn, preset, reset
  D_Flip_Flop d_ff_3 (.D(moore2_next_1_ns3), .clk(clock_1_out), .Q(d_ff_3_q));  // open: Qn, preset, reset
  D_Flip_Flop d_ff_4 (.D(moore2_next_1_ns4), .clk(clock_1_out), .Q(d_ff_4_q));  // open: Qn, preset, reset
  D_Flip_Flop d_ff_5 (.D(moore2_next_1_ns5), .clk(clock_1_out), .Q(d_ff_5_q));  // open: Qn, preset, reset
  Clock clock_1 (.out(clock_1_out));
  moore2_out moore2_out_1 (.ps1(d_ff_1_q), .ps2(d_ff_2_q), .ps3(d_ff_3_q), .ps4(d_ff_4_q), .ps5(d_ff_5_q), .out(o));
endmodule

module mealy1_next (
  input  ps1,
  input  ps2,
  input  i,
  output ns1,
  output ns2
);

  wire and_1_out, and_2_out, and_3_out, not_1_out, not_2_out, not_3_out, not_4_out, not_5_out;

  not not_1 (not_1_out, ps1);
  not not_2 (not_2_out, i);
  not not_3 (not_3_out, ps2);
  not not_4 (not_4_out, i);
  not not_5 (not_5_out, ps2);
  and and_1 (and_1_out, not_1_out, ps2, not_2_out);
  and and_2 (and_2_out, ps1, not_3_out, not_4_out);
  and and_3 (and_3_out, ps1, not_5_out);
  or or_1 (ns1, and_1_out, and_2_out);
  or or_2 (ns2, i, and_3_out);
endmodule

module mealy1_out (
  input  ps1,
  input  ps2,
  input  i,
  output out
);

  and and_1 (out, ps1, ps2, i);
endmodule

module mealy1 (
  input  i,
  output o
);

  wire clock_1_out, d_ff_1_q, d_ff_2_q, mealy1_next_1_ns1, mealy1_next_1_ns2;

  mealy1_next mealy1_next_1 (.ps1(d_ff_1_q), .ps2(d_ff_2_q), .i(i), .ns1(mealy1_next_1_ns1), .ns2(mealy1_next_1_ns2));
  Clock clock_1 (.out(clock_1_out));
  D_Flip_Flop d_ff_1 (.D(mealy1_next_1_ns1), .clk(clock_1_out), .Q(d_ff_1_q));  // open: Qn, preset, reset
  D_Flip_Flop d_ff_2 (.D(mealy1_next_1_ns2), .clk(clock_1_out), .Q(d_ff_2_q));  // open: Qn, preset, reset
  mealy1_out mealy1_out_1 (.ps1(d_ff_1_q), .ps2(d_ff_2_q), .i(i), .out(o));
endmodule

module mealy2_next (
  input  ps1,
  input  ps2,
  input  ps3,
  input  ps4,
  input  i,
  output ns1,
  output ns2,
  output ns3,
  output ns4
);

  wire not_1_out, not_2_out, not_3_out, not_4_out, not_5_out;

  not not_1 (not_1_out, i);
  not not_2 (not_2_out, i);
  not not_3 (not_3_out, ps2);
  not not_4 (not_4_out, ps3);
  not not_5 (not_5_out, i);
  and and_1 (ns1, ps2, not_1_out);
  and and_2 (ns2, ps3, not_2_out);
  and and_3 (ns4, not_3_out, not_4_out, not_5_out);

  assign ns3 = i;
endmodule

module mealy2_out (
  input  ps1,
  input  ps2,
  input  ps3,
  input  ps4,
  input  i,
  output out
);

  and and_1 (out, ps1, i);
endmodule

module mealy2 (
  input  i,
  output o
);

  wire clock_1_out, d_ff_1_q, d_ff_2_q, d_ff_3_q, d_ff_4_q, mealy2_next_1_ns1, mealy2_next_1_ns2,
       mealy2_next_1_ns3, mealy2_next_1_ns4;

  mealy2_next mealy2_next_1 (
    .ps1(d_ff_1_q), .ps2(d_ff_2_q), .ps3(d_ff_3_q), .ps4(d_ff_4_q), .i(i), .ns1(mealy2_next_1_ns1),
    .ns2(mealy2_next_1_ns2), .ns3(mealy2_next_1_ns3), .ns4(mealy2_next_1_ns4));
  Clock clock_1 (.out(clock_1_out));
  D_Flip_Flop d_ff_1 (.D(mealy2_next_1_ns1), .clk(clock_1_out), .Q(d_ff_1_q));  // open: Qn, preset, reset
  D_Flip_Flop d_ff_2 (.D(mealy2_next_1_ns2), .clk(clock_1_out), .Q(d_ff_2_q));  // open: Qn, preset, reset
  D_Flip_Flop d_ff_3 (.D(mealy2_next_1_ns3), .clk(clock_1_out), .Q(d_ff_3_q));  // open: Qn, preset, reset
  D_Flip_Flop d_ff_4 (.D(mealy2_next_1_ns4), .clk(clock_1_out), .Q(d_ff_4_q));  // open: Qn, preset, reset
  mealy2_out mealy2_out_1 (.ps1(d_ff_1_q), .ps2(d_ff_2_q), .ps3(d_ff_3_q), .ps4(d_ff_4_q), .i(i), .out(o));
endmodule
